// Logisim project projeto.circ as structural Verilog: 25 circuits, main circuit Segmentos
// SEG
module Segmentos (
  input  A,
  input  B,
  input  C,
  input  D,
  output a_2,
  output b_2,
  output c_2,
  output d_2
);

  wire and_2_out, and_3_out, and_4_out, and_5_out, and_6_out, and_7_out, and_8_out, not_1_out, not_2_out,
       not_3_out, not_4_out, not_5_out, not_6_out, not_7_out, not_8_out, not_9_out, not_10_out, not_11_out;

  not not_1 (not_1_out, B);
  not not_2 (not_2_out, C);
  not not_3 (not_3_out, D);
  not not_4 (not_4_out, A);
  not not_5 (not_5_out, C);
  not not_6 (not_6_out, D);
  not not_7 (not_7_out, B);
  not not_8 (not_8_out, B);
  not not_9 (not_9_out, A);
  not not_10 (not_10_out, D);
  not not_11 (not_11_out, C);
  and and_1 (a_2, A, not_1_out, not_2_out, not_3_out);
  and and_2 (and_2_out, not_4_out, B);
  and and_3 (and_3_out, B, not_5_out, not_6_out);
  and and_4 (and_4_out, A, not_7_out, D);
  and and_5 (and_5_out, A, not_8_out, C);
  and and_6 (and_6_out, not_9_out, C);
  and and_7 (and_7_out, C, not_10_out);
  and and_8 (and_8_out, A, not_11_out, D);
  or or_1 (b_2, and_2_out, and_3_out, and_4_out, and_5_out);
  or or_2 (c_2, and_6_out, and_7_out, and_8_out);

  assign d_2 = D;
endmodule

module Controle (
  input  [3:0] in_1,
  output [3:0] out_2
);

  wire and_1_out, and_2_out, and_3_out, and_4_out, and_5_out, and_6_out, and_7_out, not_1_out, not_2_out,
       not_3_out, not_4_out, not_5_out, not_6_out, not_7_out;

  and and_1 (and_1_out, in_1[2], in_1[1], in_1[0]);
  and and_2 (and_2_out, in_1[3], not_1_out);
  not not_1 (not_1_out, in_1[0]);
  not not_2 (not_2_out, in_1[2]);
  and and_3 (and_3_out, not_2_out, in_1[1], in_1[0]);
  and and_4 (and_4_out, in_1[2], not_3_out);
  not not_3 (not_3_out, in_1[1]);
  and and_5 (and_5_out, in_1[2], not_4_out);
  not not_4 (not_4_out, in_1[0]);
  not not_5 (not_5_out, in_1[3]);
  and and_6 (and_6_out, not_5_out, not_6_out, in_1[0]);
  not not_6 (not_6_out, in_1[1]);
  and and_7 (and_7_out, in_1[1], not_7_out);
  not not_7 (not_7_out, in_1[0]);
  not not_8 (out_2[0], in_1[0]);
  or or_1 (out_2[3], and_1_out, and_2_out);
  or or_2 (out_2[2], and_3_out, and_4_out, and_5_out);
  or or_3 (out_2[1], and_6_out, and_7_out);
endmodule

// CUS
module Controle_Unidade_Segundos (
  input  [3:0] in_1,
  output [3:0] out_2
);

  wire and_1_out, and_2_out, and_3_out, and_4_out, and_5_out, and_6_out, and_7_out, and_8_out, not_1_out,
       not_2_out, not_3_out, not_4_out, not_5_out, not_6_out, not_7_out, not_8_out;

  not not_1 (not_1_out, in_1[3]);
  not not_2 (not_2_out, in_1[2]);
  not not_3 (not_3_out, in_1[1]);
  not not_4 (not_4_out, in_1[0]);
  not not_5 (not_5_out, in_1[0]);
  not not_6 (not_6_out, in_1[1]);
  not not_7 (not_7_out, in_1[0]);
  not not_8 (not_8_out, in_1[0]);
  not not_9 (out_2[0], in_1[0]);
  and and_1 (and_1_out, not_1_out, not_2_out, not_3_out, not_4_out);
  and and_2 (and_2_out, in_1[3], in_1[0]);
  and and_3 (and_3_out, in_1[2], in_1[0]);
  and and_4 (and_4_out, in_1[2], in_1[1]);
  and and_5 (and_5_out, in_1[3], not_5_out);
  and and_6 (and_6_out, in_1[1], in_1[0]);
  and and_7 (and_7_out, in_1[2], not_6_out, not_7_out);
  and and_8 (and_8_out, in_1[3], not_8_out);
  or or_1 (out_2[3], and_1_out, and_2_out);
  or or_2 (out_2[2], and_3_out, and_4_out, and_5_out);
  or or_3 (out_2[1], and_6_out, and_7_out, and_8_out);
endmodule

// CDS
module Controle_Dezena_Segundos (
  input  [3:0] in_1,
  output [3:0] out_2
);

  wire and_1_out, and_2_out, and_3_out, and_4_out, not_1_out, not_2_out, not_3_out, not_4_out;

  not not_1 (not_1_out, in_1[2]);
  not not_2 (not_2_out, in_1[1]);
  not not_3 (not_3_out, in_1[0]);
  not not_4 (not_4_out, in_1[0]);
  not not_5 (out_2[0], in_1[0]);
  and and_1 (and_1_out, not_1_out, not_2_out, not_3_out);
  and and_2 (and_2_out, in_1[2], in_1[0]);
  and and_3 (and_3_out, in_1[1], in_1[0]);
  and and_4 (and_4_out, in_1[2], not_4_out);
  or or_1 (out_2[2], and_1_out, and_2_out);
  or or_2 (out_2[1], and_3_out, and_4_out);

  assign out_2[3] = in_1[3];
  // also tied to GND on the sheet: in_1[3]
endmodule

// CUM
module Controle_Unidade_Minutos (
  input  [3:0] in_1,
  output [3:0] out_2
);

  wire and_1_out, and_2_out, and_3_out, and_4_out, and_5_out, and_6_out, and_7_out, and_8_out, not_1_out,
       not_2_out, not_3_out, not_4_out, not_5_out, not_6_out, not_7_out, not_8_out;

  not not_1 (not_1_out, in_1[3]);
  not not_2 (not_2_out, in_1[2]);
  not not_3 (not_3_out, in_1[1]);
  not not_4 (not_4_out, in_1[0]);
  not not_5 (not_5_out, in_1[0]);
  not not_6 (not_6_out, in_1[1]);
  not not_7 (not_7_out, in_1[0]);
  not not_8 (not_8_out, in_1[0]);
  not not_9 (out_2[0], in_1[0]);
  and and_1 (and_1_out, not_1_out, not_2_out, not_3_out, not_4_out);
  and and_2 (and_2_out, in_1[3], in_1[0]);
  and and_3 (and_3_out, in_1[2], in_1[0]);
  and and_4 (and_4_out, in_1[2], in_1[1]);
  and and_5 (and_5_out, in_1[3], not_5_out);
  and and_6 (and_6_out, in_1[1], in_1[0]);
  and and_7 (and_7_out, in_1[2], not_6_out, not_7_out);
  and and_8 (and_8_out, in_1[3], not_8_out);
  or or_1 (out_2[3], and_1_out, and_2_out);
  or or_2 (out_2[2], and_3_out, and_4_out, and_5_out);
  or or_3 (out_2[1], and_6_out, and_7_out, and_8_out);
endmodule

// CDM
module Controle_Dezena_Minutos (
  input  [3:0] in_1,
  output [3:0] out_2
);

  wire and_1_out, and_2_out, and_3_out, and_4_out, not_1_out, not_2_out, not_3_out, not_4_out;

  not not_1 (not_1_out, in_1[2]);
  not not_2 (not_2_out, in_1[1]);
  not not_3 (not_3_out, in_1[0]);
  not not_4 (not_4_out, in_1[0]);
  not not_5 (out_2[0], in_1[0]);
  and and_1 (and_1_out, not_1_out, not_2_out, not_3_out);
  and and_2 (and_2_out, in_1[2], in_1[0]);
  and and_3 (and_3_out, in_1[1], in_1[0]);
  and and_4 (and_4_out, in_1[2], not_4_out);
  or or_1 (out_2[2], and_1_out, and_2_out);
  or or_2 (out_2[1], and_3_out, and_4_out);

  assign out_2[3] = in_1[3];
  // also tied to GND on the sheet: in_1[3]
endmodule

// CTC
module Controle_Configurar (
  input  A,
  output a_2
);

  not not_1 (a_2, A);
endmodule

module Teste (
  input  CFG,
  input  CLOCK,
  input  dmb,
  input  dma,
  output out_5
);

  wire and_1_out, and_2_out;

  and and_1 (and_1_out, CFG, dma);
  and and_2 (and_2_out, CFG, dmb);
  or or_1 (out_5, CLOCK, and_1_out, and_2_out);
endmodule

module Brains (
  input  dma,
  input  dmb,
  input  CFG,
  input  CLOCK,
  output out_5
);

  wire and_1_out, and_2_out, and_3_out, or_1_out;

  or or_1 (or_1_out, dma, dmb);
  and and_1 (and_1_out, ~CFG, CLOCK);  // AND_Gate
  and and_2 (and_2_out, CFG, or_1_out);
  and and_3 (and_3_out, or_1_out, and_1_out);
  or or_2 (out_5, and_2_out, and_3_out, and_1_out);
endmodule

// CFG
module Config (
  input  E,
  output S
);

  wire controle_configurar_1_a_2;

  D_Flip_Flop d_ff_1 (.clk(E), .D(controle_configurar_1_a_2), .Q(S), .en(1'b1));  // open: Qn, preset, reset
  Controle_Configurar controle_configurar_1 (.A(S), .a_2(controle_configurar_1_a_2));
endmodule

// US
module Unidade_Segundo (
  input  CLEAR,
  input  usa,
  input  usb,
  input  CFG,
  input  CLOCK,
  input  ENABLE,
  input  PRESET,
  output CLK,
  output [3:0] DISPLAY_U1
);

  wire brains_1_out_5;
  wire [3:0] d_ff_4_q;

  Brains brains_1 (.dma(usa), .dmb(usb), .CFG(CFG), .CLOCK(CLOCK), .out_5(brains_1_out_5));
  D_Flip_Flop d_ff_1 (
    .clk(brains_1_out_5), .D(DISPLAY_U1[3]), .Q(d_ff_4_q[3]), .preset(PRESET), .en(ENABLE), .reset(CLEAR));  // open: Qn
  and and_1 (CLK, ~d_ff_4_q[3], ~d_ff_4_q[2], ~d_ff_4_q[1], ~d_ff_4_q[0]);  // AND_Gate
  D_Flip_Flop d_ff_2 (
    .clk(brains_1_out_5), .D(DISPLAY_U1[2]), .Q(d_ff_4_q[2]), .preset(PRESET), .en(ENABLE), .reset(CLEAR));  // open: Qn
  D_Flip_Flop d_ff_3 (
    .clk(brains_1_out_5), .D(DISPLAY_U1[1]), .Q(d_ff_4_q[1]), .preset(PRESET), .en(ENABLE), .reset(CLEAR));  // open: Qn
  D_Flip_Flop d_ff_4 (
    .clk(brains_1_out_5), .D(DISPLAY_U1[0]), .Q(d_ff_4_q[0]), .preset(PRESET), .en(ENABLE), .reset(CLEAR));  // open: Qn
  Controle_Unidade_Segundos controle_unidade_segundos_1 (.in_1(d_ff_4_q), .out_2(DISPLAY_U1));
endmodule

// DS
module Dezena_Segundo (
  input  CLEAR,
  input  dsa,
  input  dsb,
  input  CFG,
  input  CLOCK,
  input  ENABLE,
  input  PRESET,
  output CLK,
  output [3:0] DISPLAY_U2
);

  wire brains_1_out_5;
  wire [3:0] d_ff_4_q;

  Brains brains_1 (.dma(dsa), .dmb(dsb), .CFG(CFG), .CLOCK(CLOCK), .out_5(brains_1_out_5));
  D_Flip_Flop d_ff_1 (
    .clk(brains_1_out_5), .D(DISPLAY_U2[3]), .Q(d_ff_4_q[3]), .preset(PRESET), .en(ENABLE), .reset(CLEAR));  // open: Qn
  and and_1 (CLK, ~d_ff_4_q[3], ~d_ff_4_q[2], ~d_ff_4_q[1], ~d_ff_4_q[0]);  // AND_Gate
  D_Flip_Flop d_ff_2 (
    .clk(brains_1_out_5), .D(DISPLAY_U2[2]), .Q(d_ff_4_q[2]), .preset(PRESET), .en(ENABLE), .reset(CLEAR));  // open: Qn
  D_Flip_Flop d_ff_3 (
    .clk(brains_1_out_5), .D(DISPLAY_U2[1]), .Q(d_ff_4_q[1]), .preset(PRESET), .en(ENABLE), .reset(CLEAR));  // open: Qn
  D_Flip_Flop d_ff_4 (
    .clk(brains_1_out_5), .D(DISPLAY_U2[0]), .Q(d_ff_4_q[0]), .preset(PRESET), .en(ENABLE), .reset(CLEAR));  // open: Qn
  Controle_Dezena_Segundos controle_dezena_segundos_1 (.in_1(d_ff_4_q), .out_2(DISPLAY_U2));
endmodule

// UM
module Unidade_Minuto (
  input  CLEAR,
  input  uma,
  input  umb,
  input  CFG,
  input  CLOCK,
  input  ENABLE,
  input  PRESET,
  output CLK,
  output [3:0] DISPLAY_M1
);

  wire brains_1_out_5;
  wire [3:0] d_ff_4_q;

  Brains brains_1 (.dma(uma), .dmb(umb), .CFG(CFG), .CLOCK(CLOCK), .out_5(brains_1_out_5));
  D_Flip_Flop d_ff_1 (
    .clk(brains_1_out_5), .D(DISPLAY_M1[3]), .Q(d_ff_4_q[3]), .preset(PRESET), .en(ENABLE), .reset(CLEAR));  // open: Qn
  D_Flip_Flop d_ff_2 (
    .clk(brains_1_out_5), .D(DISPLAY_M1[2]), .Q(d_ff_4_q[2]), .preset(PRESET), .en(ENABLE), .reset(CLEAR));  // open: Qn
  and and_1 (CLK, ~d_ff_4_q[3], ~d_ff_4_q[2], ~d_ff_4_q[1], ~d_ff_4_q[0]);  // AND_Gate
  D_Flip_Flop d_ff_3 (
    .clk(brains_1_out_5), .D(DISPLAY_M1[1]), .Q(d_ff_4_q[1]), .preset(PRESET), .en(ENABLE), .reset(CLEAR));  // open: Qn
  D_Flip_Flop d_ff_4 (
    .clk(brains_1_out_5), .D(DISPLAY_M1[0]), .Q(d_ff_4_q[0]), .preset(PRESET), .en(ENABLE), .reset(CLEAR));  // open: Qn
  Controle_Unidade_Minutos controle_unidade_minutos_1 (.in_1(d_ff_4_q), .out_2(DISPLAY_M1));
endmodule

// DM
module Dezena_Minuto (
  input  CLEAR,
  input  dma,
  input  dmb,
  input  CFG,
  input  CLOCK,
  input  ENABLE,
  input  PRESET,
  output CLK,
  output [3:0] DISPLAY_M2
);

  wire brains_1_out_5;
  wire [3:0] d_ff_4_q;

  Brains brains_1 (.dma(dma), .dmb(dmb), .CFG(CFG), .CLOCK(CLOCK), .out_5(brains_1_out_5));
  D_Flip_Flop d_ff_1 (
    .clk(brains_1_out_5), .D(DISPLAY_M2[3]), .Q(d_ff_4_q[3]), .preset(PRESET), .en(ENABLE), .reset(CLEAR));  // open: Qn
  D_Flip_Flop d_ff_2 (
    .clk(brains_1_out_5), .D(DISPLAY_M2[2]), .Q(d_ff_4_q[2]), .preset(PRESET), .en(ENABLE), .reset(CLEAR));  // open: Qn
  and and_1 (CLK, ~d_ff_4_q[3], ~d_ff_4_q[2], ~d_ff_4_q[1], ~d_ff_4_q[0]);  // AND_Gate
  D_Flip_Flop d_ff_3 (
    .clk(brains_1_out_5), .D(DISPLAY_M2[1]), .Q(d_ff_4_q[1]), .preset(PRESET), .en(ENABLE), .reset(CLEAR));  // open: Qn
  D_Flip_Flop d_ff_4 (
    .clk(brains_1_out_5), .D(DISPLAY_M2[0]), .Q(d_ff_4_q[0]), .preset(PRESET), .en(ENABLE), .reset(CLEAR));  // open: Qn
  Controle_Dezena_Minutos controle_dezena_minutos_1 (.in_1(d_ff_4_q), .out_2(DISPLAY_M2));
endmodule

// G1
module Gerador_1 (
  input  CLOCK,
  output [3:0] out_2
);

  Random #(.width(4)) random_1 (.clk(CLOCK), .next(1'b1), .out(out_2));  // open: clr
endmodule

// G2
module Gerador_2 (
  input  CLOCK,
  output [3:0] out_2
);

  Random #(.width(4)) random_1 (.clk(CLOCK), .next(1'b1), .out(out_2));  // open: clr
endmodule

// CEA
module Controle_Estados_A (
  input  [3:0] Entrada,
  output [3:0] \Saída 
);

  wire not_1_out, not_2_out, not_3_out, not_4_out, not_5_out;

  not not_1 (not_1_out, Entrada[2]);
  not not_2 (not_2_out, Entrada[1]);
  not not_3 (not_3_out, Entrada[2]);
  not not_4 (not_4_out, Entrada[1]);
  not not_5 (not_5_out, Entrada[0]);
  and and_1 (\Saída [1], not_1_out, not_2_out, Entrada[0]);
  and and_2 (\Saída [0], not_3_out, not_4_out, not_5_out);

  assign \Saída [3:2] = {Entrada[3], 1'b0};
  // also tied to GND on the sheet: Entrada[3]
endmodule

// CEB
module Controle_Estados_B (
  input  [3:0] in_1,
  output [3:0] out_2
);

  wire and_1_out, and_2_out, and_3_out, and_4_out, and_5_out, not_1_out, not_2_out, not_3_out, not_4_out,
       not_5_out, not_6_out, not_7_out, not_8_out;

  not not_1 (not_1_out, in_1[0]);
  not not_2 (not_2_out, in_1[2]);
  not not_3 (not_3_out, in_1[1]);
  not not_4 (not_4_out, in_1[2]);
  not not_5 (not_5_out, in_1[0]);
  not not_6 (not_6_out, in_1[1]);
  not not_7 (not_7_out, in_1[1]);
  not not_8 (not_8_out, in_1[0]);
  and and_1 (and_1_out, in_1[1], in_1[0]);
  and and_2 (and_2_out, in_1[2], not_1_out);
  and and_3 (and_3_out, not_2_out, not_3_out);
  and and_4 (and_4_out, not_4_out, not_5_out);
  and and_5 (and_5_out, not_6_out, in_1[0]);
  or or_1 (out_2[0], not_7_out, not_8_out);
  or or_2 (out_2[2], and_1_out, and_2_out);
  or or_3 (out_2[1], and_3_out, and_4_out, and_5_out);

  assign out_2[3] = in_1[3];
  // also tied to GND on the sheet: in_1[3]
endmodule

// CTE
module Controle_Estados (
  input  [3:0] in_1,
  output [3:0] out_2
);

  wire and_1_out, and_2_out, and_3_out, and_4_out, not_1_out, not_2_out, not_3_out, not_4_out;

  not not_1 (not_1_out, in_1[0]);
  not not_2 (not_2_out, in_1[2]);
  not not_3 (not_3_out, in_1[1]);
  not not_4 (not_4_out, in_1[0]);
  not not_5 (out_2[0], in_1[0]);
  and and_1 (and_1_out, in_1[1], in_1[0]);
  and and_2 (and_2_out, in_1[2], not_1_out);
  and and_3 (and_3_out, not_2_out, not_3_out, in_1[0]);
  and and_4 (and_4_out, in_1[1], not_4_out);
  or or_1 (out_2[2], and_1_out, and_2_out);
  or or_2 (out_2[1], and_3_out, and_4_out);

  assign out_2[3] = in_1[3];
  // also tied to GND on the sheet: in_1[3]
endmodule

module \Circuito___Próximo  (
  input  [3:0] in_1,
  output xA,
  output yA,
  output rA,
  output xB,
  output yB,
  output rB
);

  wire not_1_out, not_2_out, not_3_out, not_4_out, not_5_out, not_6_out, not_7_out;

  not not_1 (not_1_out, in_1[2]);
  not not_2 (not_2_out, in_1[1]);
  not not_3 (not_3_out, in_1[0]);
  not not_4 (not_4_out, in_1[2]);
  not not_5 (not_5_out, in_1[1]);
  not not_6 (not_6_out, in_1[0]);
  and and_1 (xB, in_1[1], in_1[0]);
  not not_7 (not_7_out, in_1[0]);
  and and_2 (rB, in_1[2], in_1[0]);
  and and_3 (xA, not_1_out, not_2_out, not_3_out);
  and and_4 (yA, not_4_out, not_5_out, in_1[0]);
  and and_5 (rA, in_1[1], not_6_out);
  and and_6 (yB, in_1[2], not_7_out);
endmodule

// ESTADOS
module Estados (
  input  CLEAR,
  input  \PRÓXIMO ,
  input  ENABLE,
  input  PRESET,
  input  endA,
  input  endB,
  output xA,
  output yA,
  output rA,
  output xB,
  output yB,
  output rB
);

  wire or_1_out;
  wire [3:0] and_1_out, and_2_out, and_3_out, bit_extender_1_out, bit_extender_2_out, bit_extender_3_out,
       controle_estados_1_out_2, \controle_estados_a_1_saída , controle_estados_b_1_out_2, d_ff_4_q, or_2_out;

  D_Flip_Flop d_ff_1 (
    .clk(\PRÓXIMO ), .D(or_2_out[3]), .Q(d_ff_4_q[3]), .preset(PRESET), .en(ENABLE), .reset(CLEAR));  // open: Qn
  D_Flip_Flop d_ff_2 (
    .clk(\PRÓXIMO ), .D(or_2_out[2]), .Q(d_ff_4_q[2]), .preset(PRESET), .en(ENABLE), .reset(CLEAR));  // open: Qn
  D_Flip_Flop d_ff_3 (
    .clk(\PRÓXIMO ), .D(or_2_out[1]), .Q(d_ff_4_q[1]), .preset(PRESET), .en(ENABLE), .reset(CLEAR));  // open: Qn
  D_Flip_Flop d_ff_4 (
    .clk(\PRÓXIMO ), .D(or_2_out[0]), .Q(d_ff_4_q[0]), .preset(PRESET), .en(ENABLE), .reset(CLEAR));  // open: Qn
  or or_1 (or_1_out, endB, endA);
  \Circuito___Próximo  \circuito_próximo_1  (.in_1(d_ff_4_q), .xA(xA), .yA(yA), .rA(rA), .xB(xB), .yB(yB), .rB(rB));
  Controle_Estados_A controle_estados_a_1 (.Entrada(d_ff_4_q), .\Saída (\controle_estados_a_1_saída ));
  Controle_Estados controle_estados_1 (.in_1(d_ff_4_q), .out_2(controle_estados_1_out_2));
  assign bit_extender_1_out = {{3{or_1_out}}, or_1_out};  // Bit_Extender bit_extender_1
  assign and_1_out = ~bit_extender_1_out & controle_estados_1_out_2;  // AND_Gate and_1, 4 bits wide
  Controle_Estados_B controle_estados_b_1 (.in_1(d_ff_4_q), .out_2(controle_estados_b_1_out_2));
  assign or_2_out = and_1_out | and_3_out | and_2_out;  // OR_Gate or_2, 4 bits wide
  assign bit_extender_2_out = {{3{endB}}, endB};  // Bit_Extender bit_extender_2
  assign and_2_out = bit_extender_2_out & \controle_estados_a_1_saída ;  // AND_Gate and_2, 4 bits wide
  assign bit_extender_3_out = {{3{endA}}, endA};  // Bit_Extender bit_extender_3
  assign and_3_out = bit_extender_3_out & controle_estados_b_1_out_2;  // AND_Gate and_3, 4 bits wide
endmodule

// P1
module Placar_1 (
  input  CLEAR,
  input  CLOCK,
  input  ENABLE,
  input  PRESET,
  output [3:0] DISPLAY_P1
);

  wire [3:0] adder_1_out;

  D_Flip_Flop d_ff_1 (
    .clk(CLOCK), .D(adder_1_out[3]), .Q(DISPLAY_P1[3]), .preset(PRESET), .en(ENABLE), .reset(CLEAR));  // open: Qn
  D_Flip_Flop d_ff_2 (
    .clk(CLOCK), .D(adder_1_out[2]), .Q(DISPLAY_P1[2]), .preset(PRESET), .en(ENABLE), .reset(CLEAR));  // open: Qn
  D_Flip_Flop d_ff_3 (
    .clk(CLOCK), .D(adder_1_out[1]), .Q(DISPLAY_P1[1]), .preset(PRESET), .en(ENABLE), .reset(CLEAR));  // open: Qn
  D_Flip_Flop d_ff_4 (
    .clk(CLOCK), .D(adder_1_out[0]), .Q(DISPLAY_P1[0]), .preset(PRESET), .en(ENABLE), .reset(CLEAR));  // open: Qn
  Adder #(.width(4)) adder_1 (.a(DISPLAY_P1), .b(4'b0001), .out(adder_1_out));  // open: cin, cout
endmodule

// P2
module Placar_2 (
  input  CLEAR,
  input  CLOCK,
  input  ENABLE,
  input  PRESET,
  output [3:0] DISPLAY_P2
);

  wire [3:0] adder_1_out;

  D_Flip_Flop d_ff_1 (
    .clk(CLOCK), .D(adder_1_out[3]), .Q(DISPLAY_P2[3]), .preset(PRESET), .en(ENABLE), .reset(CLEAR));  // open: Qn
  D_Flip_Flop d_ff_2 (
    .clk(CLOCK), .D(adder_1_out[2]), .Q(DISPLAY_P2[2]), .preset(PRESET), .en(ENABLE), .reset(CLEAR));  // open: Qn
  D_Flip_Flop d_ff_3 (
    .clk(CLOCK), .D(adder_1_out[1]), .Q(DISPLAY_P2[1]), .preset(PRESET), .en(ENABLE), .reset(CLEAR));  // open: Qn
  D_Flip_Flop d_ff_4 (
    .clk(CLOCK), .D(adder_1_out[0]), .Q(DISPLAY_P2[0]), .preset(PRESET), .en(ENABLE), .reset(CLEAR));  // open: Qn
  Adder #(.width(4)) adder_1 (.a(DISPLAY_P2), .b(4'b0001), .out(adder_1_out));  // open: cin, cout
endmodule

// CORE
module Core (
  input  xA,
  input  yA,
  input  rA,
  input  cA,
  input  [4:0] G1,
  input  [3:0] Chute_Jogador_A,
  input  [4:0] G2,
  input  CHUTAR,
  input  R___ACERTOU,
  input  xB,
  input  yB,
  input  rB,
  input  cB,
  input  [3:0] Chute_Jogador_B,
  input  CHUTAR_2,
  output [3:0] XHC,
  output ACERTOU,
  output out_18,
  output out_19,
  output out_20,
  output [3:0] YHC,
  output ACERTOU_2,
  output [4:0] SG1V,
  output [4:0] SG2V
);

  wire and_3_out, and_6_out, and_7_out, and_8_out, and_12_out, comparator_1_eq, comparator_2_eq,
       comparator_2_gt, comparator_2_lt, comparator_3_eq, or_5_out, or_6_out, tunnel, tunnel_t_t,
       tunnel_t_t_t_t;
  wire [3:0] and_1_out, and_2_out, and_4_out, and_5_out, bit_extender_1_out, bit_extender_2_out,
       bit_extender_3_out, bit_extender_4_out, BXHC, BYHC, or_3_out, or_4_out, register_1_q, register_3_q;
  wire [4:0] adder_1_out, adder_2_out, bit_extender_5_out, bit_extender_6_out, bit_extender_7_out,
       bit_extender_8_out;

  assign bit_extender_1_out = {{3{xA}}, xA};  // Bit_Extender bit_extender_1
  assign bit_extender_2_out = {{3{yA}}, yA};  // Bit_Extender bit_extender_2
  assign bit_extender_3_out = {{3{xB}}, xB};  // Bit_Extender bit_extender_3
  assign bit_extender_4_out = {{3{yB}}, yB};  // Bit_Extender bit_extender_4
  assign and_1_out = bit_extender_1_out & Chute_Jogador_A;  // AND_Gate and_1, 4 bits wide
  Register #(.width(4)) register_1 (.D(and_2_out), .en(1'b1), .Q(register_1_q), .clk(and_3_out), .clr(cA));
  assign and_2_out = bit_extender_2_out & Chute_Jogador_A;  // AND_Gate and_2, 4 bits wide
  and and_3 (and_3_out, yA, CHUTAR);
  assign and_4_out = bit_extender_3_out & Chute_Jogador_B;  // AND_Gate and_4, 4 bits wide
  assign and_5_out = bit_extender_4_out & Chute_Jogador_B;  // AND_Gate and_5, 4 bits wide
  Register #(.width(4)) register_2 (.D(and_5_out), .en(1'b1), .Q(BYHC), .clk(and_6_out), .clr(cB));
  and and_6 (and_6_out, yB, CHUTAR_2);
  Register #(.width(4)) register_3 (.D(and_1_out), .en(1'b1), .Q(register_3_q), .clk(and_7_out), .clr(cA));
  and and_7 (and_7_out, xA, CHUTAR);
  assign YHC = register_1_q | BYHC;  // OR_Gate or_1, 4 bits wide
  Register #(.width(4)) register_4 (.D(and_4_out), .en(1'b1), .Q(BXHC), .clk(and_8_out), .clr(cB));
  and and_8 (and_8_out, xB, CHUTAR_2);
  assign XHC = register_3_q | BXHC;  // OR_Gate or_2, 4 bits wide
  assign or_3_out = BXHC | register_3_q;  // OR_Gate or_3, 4 bits wide
  assign or_4_out = register_1_q | BYHC;  // OR_Gate or_4, 4 bits wide
  assign bit_extender_5_out = {{1{1'b0}}, or_4_out};  // Bit_Extender bit_extender_5
  assign bit_extender_6_out = {{1{1'b0}}, or_3_out};  // Bit_Extender bit_extender_6
  Adder #(.width(5)) adder_1 (.a(bit_extender_6_out), .b(bit_extender_7_out), .out(adder_1_out));  // open: cin, cout
  assign bit_extender_7_out = {{1{1'b0}}, or_4_out};  // Bit_Extender bit_extender_7
  Adder #(.width(5)) adder_2 (.a(G1), .b(G2), .out(adder_2_out));  // open: cin, cout
  Comparator #(.width(5)) comparator_1 (.a(bit_extender_5_out), .b(G2), .eq(comparator_1_eq));  // open: gt, lt
  Comparator #(.width(5)) comparator_2 (
    .a(adder_1_out), .b(adder_2_out), .gt(comparator_2_gt), .eq(comparator_2_eq), .lt(comparator_2_lt));
  D_Flip_Flop d_ff_1 (
    .clk(tunnel_t_t_t_t), .D(tunnel_t_t_t_t), .Q(out_18), .en(1'b1), .reset(R___ACERTOU));  // open: Qn, preset
  D_Flip_Flop d_ff_2 (
    .clk(tunnel_t_t), .D(tunnel_t_t), .Q(out_19), .en(1'b1), .reset(R___ACERTOU));  // open: Qn, preset
  D_Flip_Flop d_ff_3 (.clk(tunnel), .D(tunnel), .Q(out_20), .en(1'b1), .reset(R___ACERTOU));  // open: Qn, preset
  or or_5 (or_5_out, rA, rB);
  and and_9 (tunnel_t_t_t_t, comparator_2_gt, or_5_out);
  and and_10 (tunnel_t_t, comparator_2_eq, or_5_out);
  and and_11 (tunnel, comparator_2_lt, or_5_out);
  assign bit_extender_8_out = {{1{1'b0}}, or_3_out};  // Bit_Extender bit_extender_8
  Comparator #(.width(5)) comparator_3 (.a(bit_extender_8_out), .b(G1), .eq(comparator_3_eq));  // open: gt, lt
  and and_12 (and_12_out, comparator_3_eq, or_5_out, comparator_1_eq);
  or or_6 (or_6_out, xB, xA);
  D_Flip_Flop d_ff_4 (
    .clk(and_12_out), .D(and_12_out), .Q(ACERTOU_2), .en(1'b1), .reset(R___ACERTOU));  // open: Qn, preset
  and and_13 (ACERTOU, or_6_out, ACERTOU_2);

  assign SG1V = G1;
  assign SG2V = G2;

  // Other names for the same wires on the sheet: SG1[4:0] = G1; SG2[4:0] = G2; tunnel_t = out_20;
  //   tunnel_t_t_t = out_19; tunnel_t_t_t_t_t = out_18; XHCB[3:0] = BXHC; YHCB[3:0] = BYHC
endmodule

module Projeto_Final (
  input  in_1,
  input  in_2,
  input  in_3,
  input  in_4,
  input  in_5,
  input  in_6,
  input  in_7,
  input  in_8,
  output [3:0] SG1,
  output [3:0] SG2
);

  wire A___JOGANDO, A_VENCEU, A_VENCEU_1, A_VENCEU_2, ACERTOU, ACERTOU_t, and_1_out, and_2_out, and_3_out,
       and_4_out, and_5_out, and_6_out, and_8_out, and_9_out, and_11_out, and_12_out, and_15_out, and_16_out,
       and_17_out, and_18_out, B___JOGANDO, B_VENCEU, B_VENCEU_1, B_VENCEU_2, cA, cB, CHUTANDO_X, CHUTANDO_Y,
       CHUTANDO_Y___A, CHUTANDO_Y___B, CHUTAR, clock_1_out, clock_2_out, comparator_1_eq, comparator_1_gt,
       comparator_1_lt, comparator_4_gt, comparator_4_lt, comparator_5_eq, comparator_6_eq, comparator_7_eq,
       comparator_8_eq, comparator_9_eq, comparator_10_eq, comparator_11_eq, comparator_12_eq, config_3_s,
       config_4_s, CONFIGURAR, dezena_segundo_1_clk, dezena_segundo_2_clk, dma_t, dmb_t, dsa_t, dsb_t,
       EMPATE, endA, endB, FIM_DE_JOGO, FIM_DE_JOGO_A15, FIM_DE_JOGO_B15, FIM_DE_JOGO_TEMPO, FIM_DE_JOGO_X15,
       IGUAL, MAIOR, MENOR, or_1_out, or_2_out, or_3_out, or_4_out, or_11_out, or_12_out, or_18_out,
       or_19_out, or_20_out, or_21_out, \PRÓXIMO , R___Acertou, rA, rB, RESET, START, SX, SY, tunnel, uma_t,
       umb_t, unidade_minuto_1_clk, unidade_minuto_2_clk, unidade_segundo_1_clk, unidade_segundo_2_clk,
       usa_t, usb_t;
  wire [2:0] core_1_xhc, core_1_yhc;
  wire [3:0] DMA, DMB, DSA, DSB, GA, GB, gerador_1_1_out_2, gerador_2_1_out_2, PA, PB, UMA, UMB, USA, USB,
       XHC, YHC;
  wire [4:0] bit_extender_1_out, bit_extender_2_out, core_1_sg1v, core_1_sg2v;

  Config config_1 (.E(CONFIGURAR), .S(tunnel));
  Config config_2 (.E(CONFIGURAR), .S(tunnel));
  Segmentos segmentos_1 (.A(in_1), .B(in_2), .C(in_3), .D(in_4), .a_2(GA[3]), .b_2(GA[2]), .c_2(GA[1]), .d_2(GA[0]));
  and and_1 (and_1_out, A___JOGANDO, rA, ACERTOU_t);
  Segmentos segmentos_2 (.A(in_5), .B(in_6), .C(in_7), .D(in_8), .a_2(GB[3]), .b_2(GB[2]), .c_2(GB[1]), .d_2(GB[0]));
  and and_2 (and_2_out, B___JOGANDO, rB, ACERTOU_t);
  Button button_1 (.out(dma_t));
  Button button_2 (.out(uma_t));
  Hex_Digit_Display hex_digit_display_1 (.value(UMA));  // open: dp
  Hex_Digit_Display hex_digit_display_2 (.value(DMA));  // open: dp
  LED led_1 (.in(in_1));
  Dezena_Minuto dezena_minuto_1 (
    .CLEAR(RESET), .dma(dma_t), .dmb(dmb_t), .CFG(and_3_out), .CLOCK(unidade_minuto_1_clk), .ENABLE(1'b1),
    .DISPLAY_M2(DMA));  // open: PRESET, CLK
  and and_3 (and_3_out, or_1_out, tunnel);
  or or_1 (or_1_out, dmb_t, dma_t);
  Dezena_Minuto dezena_minuto_2 (
    .CLEAR(RESET), .dma(dma_t), .dmb(dmb_t), .CFG(and_4_out), .CLOCK(unidade_minuto_2_clk), .ENABLE(1'b1),
    .DISPLAY_M2(DMB));  // open: PRESET, CLK
  and and_4 (and_4_out, or_2_out, tunnel);
  or or_2 (or_2_out, dmb_t, dma_t);
  Placar_1 placar_1_1 (.CLEAR(RESET), .CLOCK(and_1_out), .ENABLE(1'b1), .DISPLAY_P1(PA));  // open: PRESET
  Placar_2 placar_2_1 (.CLEAR(RESET), .CLOCK(and_2_out), .ENABLE(1'b1), .DISPLAY_P2(PB));  // open: PRESET
  Hex_Digit_Display hex_digit_display_3 (.value(PA));  // open: dp
  Button button_3 (.out(dsa_t));
  LED led_2 (.in(1'b1));
  LED led_3 (.in(1'b1));
  Hex_Digit_Display hex_digit_display_4 (.value(DSA));  // open: dp
  Hex_Digit_Display hex_digit_display_5 (.value(GA));  // open: dp
  LED led_4 (.in(A___JOGANDO));
  LED led_5 (.in(A___JOGANDO));
  LED led_6 (.in(A___JOGANDO));
  Button button_4 (.out(usa_t));
  Hex_Digit_Display hex_digit_display_6 (.value(USA));  // open: dp
  Comparator #(.width(4)) comparator_1 (
    .a(PA), .b(PB), .gt(comparator_1_gt), .eq(comparator_1_eq), .lt(comparator_1_lt));
  Comparator #(.width(4)) comparator_2 (.a(4'b1111), .b(PA), .eq(FIM_DE_JOGO_A15));  // open: gt, lt
  Comparator #(.width(4)) comparator_3 (.a(4'b1111), .b(PB), .eq(FIM_DE_JOGO_B15));  // open: gt, lt
  Unidade_Minuto unidade_minuto_1 (
    .CLEAR(RESET), .uma(uma_t), .umb(umb_t), .CFG(and_5_out), .CLOCK(dezena_segundo_1_clk), .ENABLE(1'b1),
    .DISPLAY_M1(UMA), .CLK(unidade_minuto_1_clk));  // open: PRESET
  and and_5 (and_5_out, or_3_out, tunnel);
  or or_3 (or_3_out, uma_t, umb_t);
  Unidade_Minuto unidade_minuto_2 (
    .CLEAR(RESET), .uma(uma_t), .umb(umb_t), .CFG(and_6_out), .CLOCK(dezena_segundo_2_clk), .ENABLE(1'b1),
    .DISPLAY_M1(UMB), .CLK(unidade_minuto_2_clk));  // open: PRESET
  and and_6 (and_6_out, or_4_out, tunnel);
  or or_4 (or_4_out, uma_t, umb_t);
  or or_5 (CHUTANDO_X, cA, cB);
  or or_6 (CHUTANDO_Y, CHUTANDO_Y___B, CHUTANDO_Y___A);
  or or_7 (FIM_DE_JOGO_X15, FIM_DE_JOGO_A15, FIM_DE_JOGO_B15);
  and and_7 (FIM_DE_JOGO_TEMPO, endA, endB);
  or or_8 (FIM_DE_JOGO, A_VENCEU, FIM_DE_JOGO_X15, FIM_DE_JOGO_TEMPO, B_VENCEU);
  or or_9 (A___JOGANDO, cB, CHUTANDO_Y___A, rA);
  Estados estados_1 (
    .CLEAR(RESET), .\PRÓXIMO (\PRÓXIMO ), .ENABLE(1'b1), .endA(endA), .endB(endB), .xA(cB),
    .yA(CHUTANDO_Y___A), .rA(rA), .xB(cA), .yB(CHUTANDO_Y___B), .rB(rB));  // open: PRESET
  or or_10 (B___JOGANDO, cA, CHUTANDO_Y___B, rB);
  LED led_7 (.in(A_VENCEU));
  Button button_5 (.out(START));
  LED led_8 (.in(SX));
  and and_8 (and_8_out, FIM_DE_JOGO_TEMPO, comparator_1_gt);
  and and_9 (and_9_out, comparator_1_lt, FIM_DE_JOGO_TEMPO);
  LED led_9 (.in(MAIOR));
  Button button_6 (.out(\PRÓXIMO ));
  Hex_Digit_Display hex_digit_display_7 (.value(XHC));  // open: dp
  LED led_10 (.in(CHUTANDO_X));
  Dezena_Segundo dezena_segundo_1 (
    .CLEAR(RESET), .dsa(dsa_t), .dsb(dsb_t), .CFG(and_11_out), .CLOCK(unidade_segundo_1_clk), .ENABLE(1'b1),
    .DISPLAY_U2(DSA), .CLK(dezena_segundo_1_clk));  // open: PRESET
  Dezena_Segundo dezena_segundo_2 (
    .CLEAR(RESET), .dsa(dsa_t), .dsb(dsb_t), .CFG(and_12_out), .CLOCK(unidade_segundo_2_clk), .ENABLE(1'b1),
    .DISPLAY_U2(DSB), .CLK(dezena_segundo_2_clk));  // open: PRESET
  and and_10 (EMPATE, comparator_1_eq, FIM_DE_JOGO_TEMPO);
  Comparator #(.width(4)) comparator_4 (.a(PA), .b(PB), .gt(comparator_4_gt), .lt(comparator_4_lt));  // open: eq
  LED led_11 (.in(FIM_DE_JOGO));
  LED led_12 (.in(EMPATE));
  LED led_13 (.in(tunnel));
  Button button_7 (.out(CONFIGURAR));
  LED led_14 (.in(ACERTOU_t));
  LED led_15 (.in(IGUAL));
  Button button_8 (.out(CHUTAR));
  LED led_16 (.in(SY));
  Hex_Digit_Display hex_digit_display_8 (.value(YHC));  // open: dp
  LED led_17 (.in(CHUTANDO_Y));
  and and_11 (and_11_out, or_11_out, tunnel);
  or or_11 (or_11_out, dsb_t, dsa_t);
  and and_12 (and_12_out, or_12_out, tunnel);
  or or_12 (or_12_out, dsb_t, dsa_t);
  or or_13 (A_VENCEU_1, FIM_DE_JOGO_A15, and_8_out);
  or or_14 (B_VENCEU_1, and_9_out, FIM_DE_JOGO_B15);
  Gerador_1 gerador_1_1 (.CLOCK(ACERTOU), .out_2(gerador_1_1_out_2));
  assign bit_extender_1_out = {{1{1'b0}}, gerador_1_1_out_2};  // Bit_Extender bit_extender_1
  LED led_18 (.in(B_VENCEU));
  Button button_9 (.out(RESET));
  LED led_19 (.in(MENOR));
  or or_15 (R___Acertou, cA, cB);
  and and_13 (A_VENCEU_2, endB, comparator_4_gt);
  and and_14 (B_VENCEU_2, comparator_4_lt, endA);
  or or_16 (A_VENCEU, A_VENCEU_1, A_VENCEU_2);
  or or_17 (B_VENCEU, B_VENCEU_1, B_VENCEU_2);
  Gerador_2 gerador_2_1 (.CLOCK(ACERTOU), .out_2(gerador_2_1_out_2));
  assign bit_extender_2_out = {{1{1'b0}}, gerador_2_1_out_2};  // Bit_Extender bit_extender_2
  Unidade_Segundo unidade_segundo_1 (
    .CLEAR(RESET), .usa(usa_t), .usb(usb_t), .CFG(tunnel), .CLOCK(and_15_out), .ENABLE(1'b1),
    .DISPLAY_U1(USA), .CLK(unidade_segundo_1_clk));  // open: PRESET
  and and_15 (and_15_out, config_3_s, A___JOGANDO, and_17_out);
  Unidade_Segundo unidade_segundo_2 (
    .CLEAR(RESET), .usa(usa_t), .usb(usb_t), .CFG(tunnel), .CLOCK(and_16_out), .ENABLE(1'b1),
    .DISPLAY_U1(USB), .CLK(unidade_segundo_2_clk));  // open: PRESET
  and and_16 (and_16_out, config_4_s, B___JOGANDO, and_18_out);
  Segmentos segmentos_3 (
    .A(SX), .B(core_1_xhc[2]), .C(core_1_xhc[1]), .D(core_1_xhc[0]), .a_2(XHC[3]), .b_2(XHC[2]),
    .c_2(XHC[1]), .d_2(XHC[0]));
  Core core_1 (
    .xA(cB), .yA(CHUTANDO_Y___A), .rA(rA), .G1(bit_extender_2_out),
    .Chute_Jogador_A({in_1, in_2, in_3, in_4}), .G2(bit_extender_1_out), .CHUTAR(CHUTAR), .xB(cA),
    .yB(CHUTANDO_Y___B), .rB(rB), .Chute_Jogador_B({in_5, in_6, in_7, in_8}), .CHUTAR_2(CHUTAR),
    .XHC({SX, core_1_xhc}), .YHC({SY, core_1_yhc}), .R___ACERTOU(R___Acertou), .cA(or_20_out),
    .ACERTOU(ACERTOU), .out_18(MAIOR), .out_19(IGUAL), .out_20(MENOR), .ACERTOU_2(ACERTOU_t), .cB(or_21_out),
    .SG1V(core_1_sg1v), .SG2V(core_1_sg2v));
  Config config_3 (.E(START), .S(config_3_s));
  and and_17 (and_17_out, clock_1_out, ~or_18_out);  // AND_Gate
  Clock clock_1 (.out(clock_1_out));
  or or_18 (or_18_out, endA, FIM_DE_JOGO_X15);
  Config config_4 (.E(START), .S(config_4_s));
  and and_18 (and_18_out, clock_2_out, ~or_19_out);  // AND_Gate
  Clock clock_2 (.out(clock_2_out));
  or or_19 (or_19_out, endB, FIM_DE_JOGO_X15);
  or or_20 (or_20_out, RESET, cA);
  Segmentos segmentos_4 (
    .A(SY), .B(core_1_yhc[2]), .C(core_1_yhc[1]), .D(core_1_yhc[0]), .a_2(YHC[3]), .b_2(YHC[2]),
    .c_2(YHC[1]), .d_2(YHC[0]));
  Button button_10 (.out(umb_t));
  Button button_11 (.out(dmb_t));
  Hex_Digit_Display hex_digit_display_9 (.value(DMB));  // open: dp
  Hex_Digit_Display hex_digit_display_10 (.value(UMB));  // open: dp
  LED led_20 (.in(in_5));
  Comparator #(.width(4)) comparator_5 (.a(DMA), .b(4'b0000), .eq(comparator_5_eq));  // open: gt, lt
  Comparator #(.width(4)) comparator_6 (.a(UMA), .b(4'b0000), .eq(comparator_6_eq));  // open: gt, lt
  Comparator #(.width(4)) comparator_7 (.a(USA), .b(4'b0000), .eq(comparator_7_eq));  // open: gt, lt
  Comparator #(.width(4)) comparator_8 (.a(DSA), .b(4'b0000), .eq(comparator_8_eq));  // open: gt, lt
  Comparator #(.width(4)) comparator_9 (.a(DMB), .b(4'b0000), .eq(comparator_9_eq));  // open: gt, lt
  Comparator #(.width(4)) comparator_10 (.a(UMB), .b(4'b0000), .eq(comparator_10_eq));  // open: gt, lt
  Comparator #(.width(4)) comparator_11 (.a(USB), .b(4'b0000), .eq(comparator_11_eq));  // open: gt, lt
  Comparator #(.width(4)) comparator_12 (.a(DSB), .b(4'b0000), .eq(comparator_12_eq));  // open: gt, lt
  or or_21 (or_21_out, RESET, cB);
  Bit_Extender #(.in_width(5), .out_width(4)) bit_extender_3 (.in(core_1_sg2v), .out(SG2));
  Hex_Digit_Display hex_digit_display_11 (.value(PB));  // open: dp
  Button button_12 (.out(dsb_t));
  LED led_21 (.in(1'b1));
  LED led_22 (.in(1'b1));
  Hex_Digit_Display hex_digit_display_12 (.value(DSB));  // open: dp
  Hex_Digit_Display hex_digit_display_13 (.value(GB));  // open: dp
  LED led_23 (.in(B___JOGANDO));
  LED led_24 (.in(B___JOGANDO));
  LED led_25 (.in(B___JOGANDO));
  and and_19 (endA, comparator_5_eq, comparator_6_eq, comparator_7_eq, comparator_8_eq);
  and and_20 (endB, comparator_9_eq, comparator_10_eq, comparator_11_eq, comparator_12_eq);
  Button button_13 (.out(usb_t));
  Hex_Digit_Display hex_digit_display_14 (.value(USB));  // open: dp
  Bit_Extender #(.in_width(5), .out_width(4)) bit_extender_4 (.in(core_1_sg1v), .out(SG1));

  // Other names for the same wires on the sheet: FIM_DE_JOGO_TEMPO_A = endA; FIM_DE_JOGO_TEMPO_B = endB; A0 = in_4;
  //   ESC_A[3:0] = {in_1, in_2, in_3, in_4}; A1 = in_3; A2 = in_2; A3 = in_1; SA = in_1; B0 = in_8;
  //   ESC_B[3:0] = {in_5, in_6, in_7, in_8}; B1 = in_7; B2 = in_6; B3 = in_5; SB = in_5; CHUTANDO_X___A = cB;
  //   R___Acertou_B = cB; xA = cB; CHUTANDO_X___B = cA; R___Acertou_A = cA; xB = cA; yA = CHUTANDO_Y___A;
  //   yB = CHUTANDO_Y___B

  // Notes on the sheet:
  //   JOGADOR A
  //   PLACAR
  //   CRONÔMETRO
  //   GUESS THE NUMBER XTREME
  //   DADOS DO MODO DIFÍCIL
  //   JOGADOR B
  //   PLACAR
  //   CRONÔMETRO
endmodule
